// Logisim project Project.circ as structural Verilog: 10 circuits, main circuit Main
module Adder (
  input  [3:0] a1,
  input  [3:0] b1,
  input  [3:0] a2,
  input  [3:0] b2,
  input  [3:0] a3,
  input  [3:0] b3,
  input  [3:0] a4,
  input  [3:0] b4,
  output [3:0] c1,
  output [3:0] c2,
  output [3:0] c3,
  output [3:0] c4
);

  Adder_part #(.width(4)) adder_1 (.a(a1), .b(b1), .out(c1));  // open: cin, cout
  Adder_part #(.width(4)) adder_2 (.a(a2), .b(b2), .out(c2));  // open: cin, cout
  Adder_part #(.width(4)) adder_3 (.a(a3), .b(b3), .out(c3));  // open: cin, cout
  Adder_part #(.width(4)) adder_4 (.a(a4), .b(b4), .out(c4));  // open: cin, cout
endmodule

module Determinant (
  input  [3:0] a1,
  input  [3:0] a2,
  input  [3:0] a3,
  input  [3:0] a4,
  output [3:0] out_5,
  output out_6
);

  wire [3:0] bit_extender_1_out, bit_extender_2_out, multiplier_1_out, multiplier_2_out, subtractor_1_out,
       xor_1_out;

  Multiplier #(.width(4)) multiplier_1 (.a(a1), .b(a4), .out(multiplier_1_out));  // open: cin, cout
  Multiplier #(.width(4)) multiplier_2 (.a(a2), .b(a3), .out(multiplier_2_out));  // open: cin, cout
  Comparator #(.width(4), .mode("unsigned")) comparator_1 (
    .a(multiplier_1_out), .b(multiplier_2_out), .lt(out_6));  // open: gt, eq
  Subtractor_part #(.width(4)) subtractor_1 (
    .a(multiplier_1_out), .b(multiplier_2_out), .out(subtractor_1_out));  // open: bin, bout
  assign bit_extender_1_out = {{3{out_6}}, out_6};  // Bit_Extender bit_extender_1
  assign xor_1_out = subtractor_1_out ^ bit_extender_1_out;  // XOR_Gate xor_1, 4 bits wide
  assign bit_extender_2_out = {{3{1'b0}}, out_6};  // Bit_Extender bit_extender_2
  Adder_part #(.width(4)) adder_1 (.a(xor_1_out), .b(bit_extender_2_out), .out(out_5));  // open: cin, cout
endmodule

module _7segment (
  input  D,
  input  C,
  input  B,
  input  A,
  output a_2,
  output b_2,
  output c_2,
  output d_2,
  output e,
  output f,
  output g
);

  wire and_1_out, and_2_out, and_3_out, and_4_out, and_5_out, and_6_out, and_7_out, and_8_out, and_9_out,
       and_10_out, and_11_out, and_12_out, and_13_out, and_14_out, and_15_out, and_16_out, and_17_out,
       not_1_out, not_2_out, not_3_out, not_4_out, not_5_out, not_6_out, not_7_out, not_8_out, not_9_out,
       not_10_out, not_11_out, not_12_out, not_13_out, not_14_out, not_15_out, not_16_out, not_17_out,
       not_18_out, not_19_out, not_20_out, not_21_out, or_1_out, or_2_out, or_3_out, or_4_out, or_6_out,
       or_8_out, or_9_out, or_10_out, or_11_out, or_14_out, or_15_out;

  not not_1 (not_1_out, C);
  and and_1 (and_1_out, not_1_out, not_2_out);
  not not_2 (not_2_out, A);
  and and_2 (and_2_out, C, A);
  not not_3 (not_3_out, C);
  not not_4 (not_4_out, B);
  and and_3 (and_3_out, not_4_out, not_5_out);
  not not_5 (not_5_out, A);
  not not_6 (not_6_out, B);
  or or_1 (or_1_out, not_6_out, A);
  not not_7 (not_7_out, C);
  and and_4 (and_4_out, not_7_out, not_8_out);
  not not_8 (not_8_out, A);
  not not_9 (not_9_out, C);
  and and_5 (and_5_out, not_9_out, B);
  not not_10 (not_10_out, A);
  and and_6 (and_6_out, C, not_11_out);
  not not_11 (not_11_out, B);
  not not_12 (not_12_out, C);
  and and_7 (and_7_out, not_12_out, not_13_out);
  not not_13 (not_13_out, A);
  and and_8 (and_8_out, B, not_14_out);
  not not_14 (not_14_out, A);
  not not_15 (not_15_out, B);
  and and_9 (and_9_out, not_15_out, not_16_out);
  not not_16 (not_16_out, A);
  and and_10 (and_10_out, C, not_17_out);
  not not_17 (not_17_out, B);
  and and_11 (and_11_out, C, not_18_out);
  not not_18 (not_18_out, A);
  not not_19 (not_19_out, C);
  and and_12 (and_12_out, not_19_out, B);
  and and_13 (and_13_out, C, not_20_out);
  not not_20 (not_20_out, B);
  and and_14 (and_14_out, C, not_21_out);
  not not_21 (not_21_out, A);
  or or_2 (or_2_out, and_1_out, B);
  or or_3 (or_3_out, and_2_out, D);
  or or_4 (or_4_out, not_3_out, and_3_out);
  and and_15 (and_15_out, B, A);
  or or_5 (c_2, or_1_out, C);
  or or_6 (or_6_out, and_4_out, and_5_out);
  and and_16 (and_16_out, B, not_10_out);
  and and_17 (and_17_out, and_6_out, A);
  or or_7 (e, and_7_out, and_8_out);
  or or_8 (or_8_out, and_9_out, and_10_out);
  or or_9 (or_9_out, and_11_out, D);
  or or_10 (or_10_out, and_12_out, and_13_out);
  or or_11 (or_11_out, and_14_out, D);
  or or_12 (a_2, or_2_out, or_3_out);
  or or_13 (b_2, or_4_out, and_15_out);
  or or_14 (or_14_out, or_6_out, and_16_out);
  or or_15 (or_15_out, and_17_out, D);
  or or_16 (f, or_8_out, or_9_out);
  or or_17 (g, or_10_out, or_11_out);
  or or_18 (d_2, or_14_out, or_15_out);
endmodule

// ScalarX
module Scalar_multiplier (
  input  [3:0] in_1,
  input  [3:0] in_2,
  input  [3:0] in_3,
  input  [3:0] in_4,
  input  [3:0] in_5,
  output [3:0] out_6,
  output [3:0] out_7,
  output [3:0] out_8,
  output [3:0] out_9
);

  Multiplier #(.width(4)) multiplier_1 (.a(in_2), .b(in_1), .out(out_6));  // open: cin, cout
  Multiplier #(.width(4)) multiplier_2 (.a(in_3), .b(in_1), .out(out_7));  // open: cin, cout
  Multiplier #(.width(4)) multiplier_3 (.a(in_4), .b(in_1), .out(out_8));  // open: cin, cout
  Multiplier #(.width(4)) multiplier_4 (.a(in_5), .b(in_1), .out(out_9));  // open: cin, cout
endmodule

// Matrix-X
module Matrix_Mulitplier (
  input  [3:0] a1,
  input  [3:0] a2,
  input  [3:0] a3,
  input  [3:0] a4,
  input  [3:0] b1,
  input  [3:0] b2,
  input  [3:0] b3,
  input  [3:0] b4,
  output [3:0] out_9,
  output [3:0] out_10,
  output [3:0] out_11,
  output [3:0] out_12
);

  wire [3:0] multiplier_1_out, multiplier_2_out, multiplier_3_out, multiplier_4_out, multiplier_5_out,
       multiplier_6_out, multiplier_7_out, multiplier_8_out;

  Multiplier #(.width(4)) multiplier_1 (.a(a1), .b(b1), .out(multiplier_1_out));  // open: cin, cout
  Multiplier #(.width(4)) multiplier_2 (.a(a2), .b(b3), .out(multiplier_2_out));  // open: cin, cout
  Multiplier #(.width(4)) multiplier_3 (.a(a1), .b(b2), .out(multiplier_3_out));  // open: cin, cout
  Multiplier #(.width(4)) multiplier_4 (.a(a2), .b(b4), .out(multiplier_4_out));  // open: cin, cout
  Multiplier #(.width(4)) multiplier_5 (.a(a3), .b(b1), .out(multiplier_5_out));  // open: cin, cout
  Multiplier #(.width(4)) multiplier_6 (.a(a4), .b(b3), .out(multiplier_6_out));  // open: cin, cout
  Multiplier #(.width(4)) multiplier_7 (.a(a3), .b(b2), .out(multiplier_7_out));  // open: cin, cout
  Multiplier #(.width(4)) multiplier_8 (.a(a4), .b(b4), .out(multiplier_8_out));  // open: cin, cout
  Adder_part #(.width(4)) adder_1 (.a(multiplier_1_out), .b(multiplier_2_out), .out(out_9));  // open: cin, cout
  Adder_part #(.width(4)) adder_2 (.a(multiplier_3_out), .b(multiplier_4_out), .out(out_10));  // open: cin, cout
  Adder_part #(.width(4)) adder_3 (.a(multiplier_5_out), .b(multiplier_6_out), .out(out_11));  // open: cin, cout
  Adder_part #(.width(4)) adder_4 (.a(multiplier_7_out), .b(multiplier_8_out), .out(out_12));  // open: cin, cout
endmodule

module Transpose (
  input  [3:0] a1,
  input  [3:0] a2,
  input  [3:0] a3,
  input  [3:0] a4,
  output [3:0] out_5,
  output [3:0] out_6,
  output [3:0] out_7,
  output [3:0] out_8
);


  assign out_5 = a1;
  assign out_6 = a3;
  assign out_7 = a2;
  assign out_8 = a4;
endmodule

module Inverse (
  input  [3:0] a1,
  input  [3:0] a2,
  input  [3:0] a3,
  input  [3:0] a4,
  output [3:0] b1,
  output nb2,
  output [3:0] b2,
  output nb3,
  output [3:0] b3,
  output [3:0] b4
);

  wire comparator_1_eq, not_1_out;
  wire [3:0] bit_extender_1_out, determinant_1_out_5;

  Determinant determinant_1 (.a1(a1), .a2(a2), .a3(a3), .a4(a4), .out_5(determinant_1_out_5));  // open: out_6
  not not_1 (not_1_out, comparator_1_eq);
  Comparator #(.width(4), .mode("unsigned")) comparator_1 (
    .a(determinant_1_out_5), .b(4'b0000), .eq(comparator_1_eq));  // open: gt, lt
  assign bit_extender_1_out = {{3{not_1_out}}, not_1_out};  // Bit_Extender bit_extender_1
  assign b4 = a1 & bit_extender_1_out;  // AND_Gate and_1, 4 bits wide
  assign b2 = a2 & bit_extender_1_out;  // AND_Gate and_2, 4 bits wide
  assign b3 = a3 & bit_extender_1_out;  // AND_Gate and_3, 4 bits wide
  assign b1 = a4 & bit_extender_1_out;  // AND_Gate and_4, 4 bits wide

  assign nb2 = 1'b1;
  assign nb3 = 1'b1;
endmodule

module Subtractor (
  input  [3:0] a1,
  input  [3:0] b1,
  input  [3:0] a2,
  input  [3:0] b2,
  input  [3:0] a3,
  input  [3:0] b3,
  input  [3:0] a4,
  input  [3:0] b4,
  output [3:0] out_9,
  output out_10,
  output [3:0] out_11,
  output out_12,
  output [3:0] out_13,
  output out_14,
  output [3:0] out_15,
  output out_16
);

  wire [3:0] bit_extender_1_out, bit_extender_2_out, bit_extender_3_out, bit_extender_4_out,
       bit_extender_5_out, bit_extender_6_out, bit_extender_7_out, bit_extender_8_out, subtractor_1_out,
       subtractor_2_out, subtractor_3_out, subtractor_4_out, xor_1_out, xor_2_out, xor_3_out, xor_4_out;

  Comparator #(.width(4), .mode("unsigned")) comparator_1 (.a(a1), .b(b1), .lt(out_10));  // open: gt, eq
  Comparator #(.width(4), .mode("unsigned")) comparator_2 (.a(a2), .b(b2), .lt(out_12));  // open: gt, eq
  Comparator #(.width(4), .mode("unsigned")) comparator_3 (.a(a3), .b(b3), .lt(out_14));  // open: gt, eq
  Comparator #(.width(4), .mode("unsigned")) comparator_4 (.a(a4), .b(b4), .lt(out_16));  // open: gt, eq
  assign bit_extender_1_out = {{3{out_10}}, out_10};  // Bit_Extender bit_extender_1
  assign bit_extender_2_out = {{3{out_12}}, out_12};  // Bit_Extender bit_extender_2
  assign bit_extender_3_out = {{3{out_14}}, out_14};  // Bit_Extender bit_extender_3
  assign bit_extender_4_out = {{3{out_16}}, out_16};  // Bit_Extender bit_extender_4
  Subtractor_part #(.width(4)) subtractor_1 (.a(a1), .b(b1), .out(subtractor_1_out));  // open: bin, bout
  Subtractor_part #(.width(4)) subtractor_2 (.a(a2), .b(b2), .out(subtractor_2_out));  // open: bin, bout
  Subtractor_part #(.width(4)) subtractor_3 (.a(a3), .b(b3), .out(subtractor_3_out));  // open: bin, bout
  Subtractor_part #(.width(4)) subtractor_4 (.a(a4), .b(b4), .out(subtractor_4_out));  // open: bin, bout
  assign xor_1_out = subtractor_1_out ^ bit_extender_1_out;  // XOR_Gate xor_1, 4 bits wide
  assign xor_2_out = subtractor_2_out ^ bit_extender_2_out;  // XOR_Gate xor_2, 4 bits wide
  assign xor_3_out = subtractor_3_out ^ bit_extender_3_out;  // XOR_Gate xor_3, 4 bits wide
  assign xor_4_out = subtractor_4_out ^ bit_extender_4_out;  // XOR_Gate xor_4, 4 bits wide
  assign bit_extender_5_out = {{3{1'b0}}, out_10};  // Bit_Extender bit_extender_5
  assign bit_extender_6_out = {{3{1'b0}}, out_12};  // Bit_Extender bit_extender_6
  assign bit_extender_7_out = {{3{1'b0}}, out_14};  // Bit_Extender bit_extender_7
  assign bit_extender_8_out = {{3{1'b0}}, out_16};  // Bit_Extender bit_extender_8
  Adder_part #(.width(4)) adder_1 (.a(xor_1_out), .b(bit_extender_5_out), .out(out_9));  // open: cin, cout
  Adder_part #(.width(4)) adder_2 (.a(xor_2_out), .b(bit_extender_6_out), .out(out_11));  // open: cin, cout
  Adder_part #(.width(4)) adder_3 (.a(xor_3_out), .b(bit_extender_7_out), .out(out_13));  // open: cin, cout
  Adder_part #(.width(4)) adder_4 (.a(xor_4_out), .b(bit_extender_8_out), .out(out_15));  // open: cin, cout
endmodule

module Main (
  input  [2:0] Operation,
  input  [3:0] Input_1,
  input  [3:0] Input_2,
  input  [3:0] Input_3,
  input  [3:0] Input_4,
  input  [3:0] Scalar_Multiplier
);

  wire Control_out, determinant_1_out_6, inverse_1_nb2, inverse_1_nb3, multiplexer_5_out, multiplexer_6_out,
       multiplexer_7_out, multiplexer_8_out, n7segment_1_a_2, n7segment_1_b_2, n7segment_1_c_2,
       n7segment_1_d_2, n7segment_1_e, n7segment_1_f, n7segment_1_g, n7segment_2_a_2, n7segment_2_b_2,
       n7segment_2_c_2, n7segment_2_d_2, n7segment_2_e, n7segment_2_f, n7segment_2_g, n7segment_3_a_2,
       n7segment_3_b_2, n7segment_3_c_2, n7segment_3_d_2, n7segment_3_e, n7segment_3_f, n7segment_3_g,
       n7segment_4_a_2, n7segment_4_b_2, n7segment_4_c_2, n7segment_4_d_2, n7segment_4_e, n7segment_4_f,
       n7segment_4_g, subtractor_1_out_10, subtractor_1_out_12, subtractor_1_out_14, subtractor_1_out_16;
  wire [3:0] adder_1_c1, adder_1_c2, adder_1_c3, adder_1_c4, determinant_1_out_5, inverse_1_b1, inverse_1_b2,
       inverse_1_b3, inverse_1_b4, matrix_mulitplier_1_out_9, matrix_mulitplier_1_out_10,
       matrix_mulitplier_1_out_11, matrix_mulitplier_1_out_12, multiplexer_1_out, multiplexer_2_out,
       multiplexer_3_out, multiplexer_4_out, scalar_multiplier_1_out_6, scalar_multiplier_1_out_7,
       scalar_multiplier_1_out_8, scalar_multiplier_1_out_9, storage_1__021, storage_1_o11, storage_1_o12,
       storage_1_o22, storage_1_o31, storage_1_o32, storage_1_o41, storage_1_o42, subtractor_1_out_9,
       subtractor_1_out_11, subtractor_1_out_13, subtractor_1_out_15, transpose_1_out_5, transpose_1_out_6,
       transpose_1_out_7, transpose_1_out_8;

  Button Control (.out(Control_out));
  Storage storage_1 (
    .a1(Input_1), .a2(Input_2), .a3(Input_3), .a4(Input_4), .o12(storage_1_o12), .o11(storage_1_o11),
    .o22(storage_1_o22), ._021(storage_1__021), .o32(storage_1_o32), .o31(storage_1_o31),
    .o42(storage_1_o42), .o41(storage_1_o41), .Control(Control_out));
  Adder adder_1 (
    .a1(storage_1_o11), .b1(storage_1_o12), .a2(storage_1__021), .b2(storage_1_o22), .a3(storage_1_o31),
    .b3(storage_1_o32), .a4(storage_1_o41), .b4(storage_1_o42), .c1(adder_1_c1), .c2(adder_1_c2),
    .c3(adder_1_c3), .c4(adder_1_c4));
  Matrix_Mulitplier matrix_mulitplier_1 (
    .a1(storage_1_o11), .a2(storage_1__021), .a3(storage_1_o31), .a4(storage_1_o41), .b1(storage_1_o12),
    .b2(storage_1_o22), .b3(storage_1_o32), .b4(storage_1_o42), .out_9(matrix_mulitplier_1_out_9),
    .out_10(matrix_mulitplier_1_out_10), .out_11(matrix_mulitplier_1_out_11),
    .out_12(matrix_mulitplier_1_out_12));
  Scalar_multiplier scalar_multiplier_1 (
    .in_1(Scalar_Multiplier), .in_2(storage_1_o11), .in_3(storage_1__021), .in_4(storage_1_o31),
    .in_5(storage_1_o41), .out_6(scalar_multiplier_1_out_6), .out_7(scalar_multiplier_1_out_7),
    .out_8(scalar_multiplier_1_out_8), .out_9(scalar_multiplier_1_out_9));
  Transpose transpose_1 (
    .a1(storage_1_o11), .out_6(transpose_1_out_6), .a2(storage_1__021), .a3(storage_1_o31),
    .a4(storage_1_o41), .out_5(transpose_1_out_5), .out_7(transpose_1_out_7), .out_8(transpose_1_out_8));
  Determinant determinant_1 (
    .a1(storage_1_o11), .a2(storage_1__021), .a3(storage_1_o31), .a4(storage_1_o41),
    .out_5(determinant_1_out_5), .out_6(determinant_1_out_6));
  Inverse inverse_1 (
    .a1(storage_1_o11), .a2(storage_1__021), .a3(storage_1_o31), .a4(storage_1_o41), .b1(inverse_1_b1),
    .b2(inverse_1_b2), .b3(inverse_1_b3), .b4(inverse_1_b4), .nb2(inverse_1_nb2), .nb3(inverse_1_nb3));
  Subtractor subtractor_1 (
    .out_9(subtractor_1_out_9), .a1(storage_1_o11), .b1(storage_1_o12), .out_10(subtractor_1_out_10),
    .out_11(subtractor_1_out_11), .a2(storage_1__021), .b2(storage_1_o22), .out_12(subtractor_1_out_12),
    .out_13(subtractor_1_out_13), .a3(storage_1_o31), .b3(storage_1_o32), .out_14(subtractor_1_out_14),
    .out_15(subtractor_1_out_15), .a4(storage_1_o41), .b4(storage_1_o42), .out_16(subtractor_1_out_16));
  Multiplexer #(.select(3), .width(4)) multiplexer_1 (
    .in0(adder_1_c1), .in1(subtractor_1_out_9), .in2(matrix_mulitplier_1_out_9),
    .in3(scalar_multiplier_1_out_6), .in4(transpose_1_out_5), .in5(determinant_1_out_5), .in6(inverse_1_b1),
    .out(multiplexer_1_out), .sel(Operation));  // open: in7, en
  Multiplexer #(.select(3), .width(4)) multiplexer_2 (
    .in0(adder_1_c2), .in1(subtractor_1_out_11), .in2(matrix_mulitplier_1_out_10),
    .in3(scalar_multiplier_1_out_7), .in4(transpose_1_out_6), .in6(inverse_1_b2), .out(multiplexer_2_out),
    .sel(Operation));  // open: in5, in7, en
  Multiplexer #(.select(3), .width(4)) multiplexer_3 (
    .in0(adder_1_c3), .in1(subtractor_1_out_13), .in2(matrix_mulitplier_1_out_11),
    .in3(scalar_multiplier_1_out_8), .in4(transpose_1_out_7), .in6(inverse_1_b3), .out(multiplexer_3_out),
    .sel(Operation));  // open: in5, in7, en
  Multiplexer #(.select(3), .width(4)) multiplexer_4 (
    .in0(adder_1_c4), .in1(subtractor_1_out_15), .in2(matrix_mulitplier_1_out_12),
    .in3(scalar_multiplier_1_out_9), .in4(transpose_1_out_8), .in6(inverse_1_b4), .out(multiplexer_4_out),
    .sel(Operation));  // open: in5, in7, en
  Multiplexer #(.select(3)) multiplexer_5 (
    .in1(subtractor_1_out_10), .in5(determinant_1_out_6), .out(multiplexer_5_out), .sel(Operation));  // open: in0, in2, in3, in4, in6, in7, en
  Multiplexer #(.select(3)) multiplexer_6 (
    .in1(subtractor_1_out_14), .in6(inverse_1_nb3), .out(multiplexer_6_out), .sel(Operation));  // open: in0, in2, in3, in4, in5, in7, en
  Multiplexer #(.select(3)) multiplexer_7 (
    .in1(subtractor_1_out_12), .in6(inverse_1_nb2), .out(multiplexer_7_out), .sel(Operation));  // open: in0, in2, in3, in4, in5, in7, en
  Multiplexer #(.select(3)) multiplexer_8 (
    .in1(subtractor_1_out_16), .out(multiplexer_8_out), .sel(Operation));  // open: in0, in2, in3, in4, in5, in6, in7, en
  _7_Segment_Display u_7_segment_display_1 (.g(multiplexer_5_out));  // open: f, a, b, e, d, c, dp
  _7_Segment_Display u_7_segment_display_2 (.g(multiplexer_6_out));  // open: f, a, b, e, d, c, dp
  _7_Segment_Display u_7_segment_display_3 (
    .g(n7segment_1_g), .f(n7segment_1_f), .a(n7segment_1_a_2), .b(n7segment_1_b_2), .e(n7segment_1_e),
    .d(n7segment_1_d_2), .c(n7segment_1_c_2));  // open: dp
  _7_Segment_Display u_7_segment_display_4 (
    .g(n7segment_2_g), .f(n7segment_2_f), .a(n7segment_2_a_2), .b(n7segment_2_b_2), .e(n7segment_2_e),
    .d(n7segment_2_d_2), .c(n7segment_2_c_2));  // open: dp
  _7segment u_7segment_1 (
    .D(multiplexer_1_out[3]), .C(multiplexer_1_out[2]), .B(multiplexer_1_out[1]), .A(multiplexer_1_out[0]),
    .a_2(n7segment_1_a_2), .b_2(n7segment_1_b_2), .c_2(n7segment_1_c_2), .d_2(n7segment_1_d_2),
    .e(n7segment_1_e), .f(n7segment_1_f), .g(n7segment_1_g));
  _7segment u_7segment_2 (
    .D(multiplexer_3_out[3]), .C(multiplexer_3_out[2]), .B(multiplexer_3_out[1]), .A(multiplexer_3_out[0]),
    .a_2(n7segment_2_a_2), .b_2(n7segment_2_b_2), .c_2(n7segment_2_c_2), .d_2(n7segment_2_d_2),
    .e(n7segment_2_e), .f(n7segment_2_f), .g(n7segment_2_g));
  _7_Segment_Display u_7_segment_display_5 (.g(multiplexer_7_out));  // open: f, a, b, e, d, c, dp
  _7_Segment_Display u_7_segment_display_6 (.g(multiplexer_8_out));  // open: f, a, b, e, d, c, dp
  _7_Segment_Display u_7_segment_display_7 (
    .g(n7segment_3_g), .f(n7segment_3_f), .a(n7segment_3_a_2), .b(n7segment_3_b_2), .e(n7segment_3_e),
    .d(n7segment_3_d_2), .c(n7segment_3_c_2));  // open: dp
  _7_Segment_Display u_7_segment_display_8 (
    .g(n7segment_4_g), .f(n7segment_4_f), .a(n7segment_4_a_2), .b(n7segment_4_b_2), .e(n7segment_4_e),
    .d(n7segment_4_d_2), .c(n7segment_4_c_2));  // open: dp
  _7segment u_7segment_3 (
    .D(multiplexer_2_out[3]), .C(multiplexer_2_out[2]), .B(multiplexer_2_out[1]), .A(multiplexer_2_out[0]),
    .a_2(n7segment_3_a_2), .b_2(n7segment_3_b_2), .c_2(n7segment_3_c_2), .d_2(n7segment_3_d_2),
    .e(n7segment_3_e), .f(n7segment_3_f), .g(n7segment_3_g));
  _7segment u_7segment_4 (
    .D(multiplexer_4_out[3]), .C(multiplexer_4_out[2]), .B(multiplexer_4_out[1]), .A(multiplexer_4_out[0]),
    .a_2(n7segment_4_a_2), .b_2(n7segment_4_b_2), .c_2(n7segment_4_c_2), .d_2(n7segment_4_d_2),
    .e(n7segment_4_e), .f(n7segment_4_f), .g(n7segment_4_g));

  // Notes on the sheet:
  //   S2-T15
  //   <Aditya Suresh>
  //   <Nikhil Kottoli>
  //   <Vishal>
  //   MATRIX MANIPULATOR
  //   231CS203
  //   231CS236
  //   231CS263
  //   Output - 1
  //   Output - 3
  //   Instructions
  //   All elements are to be atmost 2 bit numbers
  //   Input 1
  //   Input3
  //   2. Press the control button atleast once to store the first Matrix.
  //   3. Now, set the operation input to your required operation's corresponding value: 
  //   000  - Addition
  //   001 - Subtraction
  //   100 - Transpose
  //   101 - Determinant
  //   110 - Inverse
  //   control button atleast once until all your outputs display 0.
  //   Input 2
  //   Input 4
  //   010 - Matrix Multiplication with another matrix
  //   011 - Matrix Multiplication with a scalar
  //   4. Now if the operation requires a second matrix, input your desired matrix into the input column.
  //   Output - 4
  //   1. Input the elements of the first matrix in the order input1,input 2,input 3,input 4 where matrix would be of the form:
  //   5. If you desire to do another operation, then reset your saved values by giving the input 0000 to all 4 inputs and press the 
  //   Output - 2
endmodule

module Storage (
  input  Control,
  input  [3:0] a1,
  input  [3:0] a2,
  input  [3:0] a3,
  input  [3:0] a4,
  output [3:0] o12,
  output [3:0] o11,
  output [3:0] o22,
  output [3:0] _021,
  output [3:0] o32,
  output [3:0] o31,
  output [3:0] o42,
  output [3:0] o41
);

  D_Flip_Flop d_ff_1 (.clk(Control), .D(a1[0]), .Q(o11[0]), .en(1'b1));  // open: Qn, preset, reset
  D_Flip_Flop d_ff_2 (.clk(Control), .D(a1[1]), .Q(o11[1]), .en(1'b1));  // open: Qn, preset, reset
  D_Flip_Flop d_ff_3 (.clk(Control), .D(a1[2]), .Q(o11[2]), .en(1'b1));  // open: Qn, preset, reset
  D_Flip_Flop d_ff_4 (.clk(Control), .D(a1[3]), .Q(o11[3]), .en(1'b1));  // open: Qn, preset, reset
  D_Flip_Flop d_ff_5 (.clk(Control), .D(a2[0]), .Q(_021[0]), .en(1'b1));  // open: Qn, preset, reset
  D_Flip_Flop d_ff_6 (.clk(Control), .D(a2[1]), .Q(_021[1]), .en(1'b1));  // open: Qn, preset, reset
  D_Flip_Flop d_ff_7 (.clk(Control), .D(a2[2]), .Q(_021[2]), .en(1'b1));  // open: Qn, preset, reset
  D_Flip_Flop d_ff_8 (.clk(Control), .D(a2[3]), .Q(_021[3]), .en(1'b1));  // open: Qn, preset, reset
  D_Flip_Flop d_ff_9 (.clk(Control), .D(a3[0]), .Q(o31[0]), .en(1'b1));  // open: Qn, preset, reset
  D_Flip_Flop d_ff_10 (.clk(Control), .D(a3[1]), .Q(o31[1]), .en(1'b1));  // open: Qn, preset, reset
  D_Flip_Flop d_ff_11 (.clk(Control), .D(a3[2]), .Q(o31[2]), .en(1'b1));  // open: Qn, preset, reset
  D_Flip_Flop d_ff_12 (.clk(Control), .D(a3[3]), .Q(o31[3]), .en(1'b1));  // open: Qn, preset, reset
  D_Flip_Flop d_ff_13 (.clk(Control), .D(a4[0]), .Q(o41[0]), .en(1'b1));  // open: Qn, preset, reset
  D_Flip_Flop d_ff_14 (.clk(Control), .D(a4[1]), .Q(o41[1]), .en(1'b1));  // open: Qn, preset, reset
  D_Flip_Flop d_ff_15 (.clk(Control), .D(a4[2]), .Q(o41[2]), .en(1'b1));  // open: Qn, preset, reset
  D_Flip_Flop d_ff_16 (.clk(Control), .D(a4[3]), .Q(o41[3]), .en(1'b1));  // open: Qn, preset, reset

  assign o12 = a1;
  assign o22 = a2;
  assign o32 = a3;
  assign o42 = a4;
endmodule
